// Logisim project firstALU_Oren.circ as structural Verilog: 3 circuits, main circuit ALU
module ALU (
  input  [3:0] A,
  input  [3:0] B,
  input  [3:0] opcode,
  output z,
  output v,
  output n,
  output c,
  output [3:0] y
);

  wire [3:0] au_1_y, lu_1_y, multiplexer_1_out, multiplexer_2_out, not_1_out, not_2_out;

  assign not_1_out = ~A;  // NOT_Gate not_1, 4 bits wide
  assign not_2_out = ~B;  // NOT_Gate not_2, 4 bits wide
  Multiplexer #(.width(4)) multiplexer_1 (
    .in0(A), .in1(not_1_out), .out(multiplexer_1_out), .sel(opcode[0]));  // open: en
  Multiplexer #(.width(4)) multiplexer_2 (
    .in0(B), .in1(not_2_out), .out(multiplexer_2_out), .sel(opcode[1]));  // open: en
  AU au_1 (.A(multiplexer_1_out), .B(multiplexer_2_out), .y(au_1_y), .cin(opcode[2]), .cout(c), .ovf(v));
  LU lu_1 (.A(A), .B(multiplexer_2_out), .f0(opcode[0]), .y(lu_1_y), .f2(opcode[2]));
  Multiplexer #(.width(4)) multiplexer_3 (.in0(au_1_y), .in1(lu_1_y), .out({n, y[2:0]}), .sel(opcode[3]));  // open: en
  nor nor_1 (z, y[0], y[1], y[2], n);

  assign y[3] = n;
endmodule

module AU (
  input  cin,
  input  [3:0] A,
  input  [3:0] B,
  output [3:0] y,
  output ovf,
  output cout
);

  wire adder_1_cout, adder_2_cout, adder_3_cout;

  Adder #(.width(1)) adder_1 (.a(A[0]), .b(B[0]), .out(y[0]), .cin(cin), .cout(adder_1_cout));
  Adder #(.width(1)) adder_2 (.a(A[1]), .b(B[1]), .out(y[1]), .cin(adder_1_cout), .cout(adder_2_cout));
  Adder #(.width(1)) adder_3 (.a(A[2]), .b(B[2]), .out(y[2]), .cin(adder_2_cout), .cout(adder_3_cout));
  Adder #(.width(1)) adder_4 (.a(A[3]), .b(B[3]), .out(y[3]), .cin(adder_3_cout), .cout(cout));
  xor xor_1 (ovf, adder_3_cout, cout);
endmodule

module LU (
  input  [3:0] A,
  input  [3:0] B,
  input  f0,
  input  f2,
  output [3:0] y
);

  wire [3:0] and_1_out, or_1_out, xor_1_out;

  assign and_1_out = A & B;  // AND_Gate and_1, 4 bits wide
  assign or_1_out = A | B;  // OR_Gate or_1, 4 bits wide
  assign xor_1_out = A ^ B;  // XOR_Gate xor_1, 4 bits wide
  Multiplexer #(.select(2), .width(4)) multiplexer_1 (
    .in0(and_1_out), .in1(or_1_out), .in2(xor_1_out), .in3(B), .out(y), .sel({f0, f2}));  // open: en
endmodule
